// Logisim project my_sap_2.circ as structural Verilog: 4 circuits, main circuit main
module main (
  input  [7:0] in_1,
  input  in_2,
  input  in_3,
  input  in_4,
  input  in_5,
  input  in_6,
  input  in_7,
  input  in_8,
  input  in_9,
  input  in_10,
  output [7:0] out_11
);

  wire e_MAR, e_RAM, s_IR;
  wire [7:0] adder_1_out, IR_out_4, MAR_out_4, ram_1_dout, tmp_out_4;

  assign out_11 = in_2 ? in_1 : 8'bz;  // Controlled_Buffer controlled_buffer_1
  my_reg IR (.i(out_11), .s(s_IR), .e(1'b1), .out_4(IR_out_4));
  control control_1 (.clk(in_8), .instr(IR_out_4), .e_MAR(e_MAR), .s_IR(s_IR), .e_RAM(e_RAM));
  my_reg R1 (.i(out_11), .s(in_4), .e(in_5), .out_4(out_11));
  RAM #(.enables("line"), .trigger("high")) ram_1 (
    .addr(MAR_out_4), .we(1'b1), .clk(in_6), .din(out_11), .dout(ram_1_dout));
  assign out_11 = e_RAM ? ram_1_dout : 8'bz;  // Controlled_Buffer controlled_buffer_2
  my_reg MAR (.i(out_11), .s(in_3), .e(e_MAR), .out_4(MAR_out_4));
  my_reg tmp (.i(out_11), .s(in_7), .e(1'b1), .out_4(tmp_out_4));
  // Probe on tmp_out_4
  Adder adder_1 (.a(out_11), .b(tmp_out_4), .out(adder_1_out));  // open: cin, cout
  my_reg acc (.i(adder_1_out), .s(in_9), .e(in_10), .out_4(out_11));
endmodule

module my_reg (
  input  [7:0] i,
  input  s,
  input  e,
  output [7:0] out_4
);

  wire [7:0] register_1_q;

  Register #(.trigger("high")) register_1 (.D(i), .clk(s), .Q(register_1_q));  // open: en, clr
  assign out_4 = e ? register_1_q : 8'bz;  // Controlled_Buffer controlled_buffer_1
endmodule

module my_clock (
  input  clk,
  output n_step,
  output e,
  output s
);

  wire button_1_out, not_1_out;
  wire [1:0] counter_1_q;

  Button button_1 (.out(button_1_out));
  not not_1 (not_1_out, e);
  Counter #(.max('h3), .width(2)) counter_1 (
    .Q(counter_1_q), .clk(clk), .clr(button_1_out));  // open: load, D, count, carry, up
  D_Flip_Flop d_ff_1 (.D(not_1_out), .clk(clk), .Q(e), .reset(button_1_out));  // open: Qn, preset
  Demultiplexer #(.select(2)) demultiplexer_1 (.in(1'b1), .sel(counter_1_q));  // open: out0, out1, out2, out3
  and and_1 (s, e, clk);
  not not_2 (n_step, e);
  // Digital_Oscilloscope digital_oscilloscope_1: pin names not known; wires that end beside it: clk, e, s, n_step, button_1_out
endmodule

module control (
  input  clk,
  input  [7:0] instr,
  output e_MAR,
  output s_IR,
  output e_RAM
);

  wire button_1_out, clk_e, clk_s, my_clock_1_n_step, step_0, step_1, step_2;
  wire [1:0] counter_1_q;

  my_clock my_clock_1 (.clk(clk), .n_step(my_clock_1_n_step), .e(clk_e), .s(clk_s));
  and and_1 (e_MAR, clk_e, step_0);
  and and_2 (e_RAM, clk_e, step_0);
  Button button_1 (.out(button_1_out));
  Counter #(.max('h3), .width(2)) counter_1 (
    .Q(counter_1_q), .clk(my_clock_1_n_step), .clr(button_1_out));  // open: load, D, count, carry, up
  Demultiplexer #(.select(2)) demultiplexer_1 (
    .out0(step_0), .out1(step_1), .out2(step_2), .out3(step_2), .in(1'b1), .sel(counter_1_q));
  and and_3 (s_IR, clk_s, step_0);
endmodule
